# Fritzing sketch remote (saved by Fritzing 0.4.2b)
breadboards: 3

parts:
  IC1 = IC, DIP package, 16 pins [chip_label=CD4051BE spacing=300mil]
  U1 = mystery part, 5 pins [chip_label=4321-ROWS spacing=300mil]
  U1_2 = mystery part, 9 pins [chip_label=123456789-Columns spacing=300mil]
  Q1 = NPN-Transistor [package="TO92 [THT]"]
  R2 = Resistor [resistance=220 package=THT]
  IC1_2 = IC, DIP package, 16 pins [chip_label=CD4051BE spacing=300mil]
  Arduino1 = Arduino
  R1 = Resistor [resistance=220 package=THT]
  Q1_2 = NPN-Transistor [package="TO92 [THT]"]
  R2_2 = Resistor [resistance=220 package=THT]
  R2_3 = Resistor [resistance=220 package=THT]

nets:
  N1: IC1.pin1, U1.pin1
  N2: IC1.pin3, Q1.E, IC1_2.pin3, Q1_2.C
  N3: IC1.pin6, Arduino1.D9
  N4: IC1.pin7, IC1.pin8, IC1_2.pin7, IC1_2.pin8, Arduino1.GND, R1.Pin_0
  N5: IC1.pin9, Arduino1.D4
  N6: IC1.pin10, Arduino1.D3
  N7: IC1.pin11, Arduino1.D2
  N8: IC1.pin12, U1.pin2
  N9: IC1.pin13, U1.pin3
  N10: IC1.pin14, U1.pin4
  N11: IC1.pin15, U1.pin5
  N12: IC1.pin16, IC1_2.pin16
  N13: U1_2.pin1, IC1_2.pin13
  N14: U1_2.pin2, IC1_2.pin14
  N15: U1_2.pin3, IC1_2.pin15
  N16: U1_2.pin4, IC1_2.pin12
  N17: U1_2.pin5, IC1_2.pin1
  N18: U1_2.pin6, IC1_2.pin5
  N19: U1_2.pin7, IC1_2.pin2
  N20: U1_2.pin8, IC1_2.pin4
  N21: U1_2.pin9, R2.Pin_0, R2_2.Pin_0
  N22: Q1.B, Arduino1.D8, R1.Pin_1, R2_3.Pin_1
  N23: Q1.C, R2.Pin_1
  N24: IC1_2.pin6, Arduino1.D10
  N25: IC1_2.pin9, IC1_2.pin11, Arduino1.D7, Arduino1.D5
  N26: IC1_2.pin10, Arduino1.D6
  N27: Q1_2.E, R2_2.Pin_1
  N28: Q1_2.B, R2_3.Pin_0

notes:
  i'm unsure ahout the transistor wiring
